// Logisim project Look Ahead Carry Generator.circ as structural Verilog: 1 circuit, main circuit main
module main (
  input  P3,
  input  G3,
  input  P2,
  input  G2,
  input  G1,
  input  P1,
  input  C1,
  output C,
  output A,
  output B
);

  wire and_1_out, and_2_out, and_3_out, and_4_out, and_5_out, and_6_out, or_1_out, or_2_out, or_3_out;

  and and_1 (and_1_out, C1, G1, P1, P3);
  and and_2 (and_2_out, P1, P1, P3);
  and and_3 (and_3_out, G2, P3);
  and and_4 (and_4_out, C1, G1, P1, P1);
  and and_5 (and_5_out, G2, P1);
  and and_6 (and_6_out, C1, G1);
  or or_1 (or_1_out, and_1_out, and_2_out, and_3_out, G3);
  or or_2 (or_2_out, and_4_out, and_5_out, G2);
  or or_3 (or_3_out, and_6_out, P1);

  assign P2 = P1;
endmodule
